# Fritzing sketch TransistorTesterSH1106Perfboard (saved by Fritzing 1.0.6)
perfboards: 2

parts:
  U1 = atmega328 [package=dip]
  R1 = Resistor [tolerance=±5% power=0.25W resistance=680 package=THT]
  R4 = Resistor [tolerance=±5% power=0.25W resistance=470k package=THT]
  R2 = Resistor [tolerance=±5% power=0.25W resistance=680 package=THT]
  R5 = Resistor [tolerance=±5% power=0.25W resistance=470k package=THT]
  R3 = Resistor [tolerance=±5% power=0.25W resistance=680 package=THT]
  R6 = Resistor [tolerance=±5% power=0.25W resistance=470k package=THT]
  C1 = Film/Foil Capacitor [capacitance=100nF voltage=35V package="5mm [THT, pp]"]
  R12 = Resistor [tolerance=±5% power=0.25W resistance=10k package=THT]
  C2 = Capacitor [package=cap-pth-small]
  C3 = Capacitor [package=cap-pth-small]
  R14 = Resistor [tolerance=±5% power=0.25W resistance=470 package=THT]
  R8 = Resistor [tolerance=±5% power=0.25W resistance=10k package=THT]
  TL431 = PNP-Transistor [package="TO92 [THT]"]
  R7 = Resistor [tolerance=±5% power=0.25W resistance=1k package=THT]
  J2 = female pin header, 4 pins [form="♀ (female)"]
  J3 = female pin header, 5 pins [form="♀ (female)"]
  R13 = Resistor [tolerance=±5% power=0.25W resistance=10k package=THT]
  C4 = Electrolytic Capacitor [capacitance=1µF voltage=35V package="100 mil [THT, electrolytic]"]
  J6 = female pin header, 3 pins [form="♀ (female)"]
  J7 = female pin header, 3 pins [form="♀ (female)"]
  HT7350 = PNP-Transistor [package="TO92 [THT]"]
  C5 = Electrolytic Capacitor [capacitance=1µF voltage=35V package="100 mil [THT, electrolytic]"]
  CD4048B2 = CD4048B [part_number=CD4048B package="DIP (Dual Inline) [THT]"]
  J9 = female pin header, 1 pin [form="♀ (female)"]
  J8 = female pin header, 1 pin [form="♀ (female)"]
  J10 = female pin header, 4 pins [form="♀ (female)"]
  J11 = female pin header, 4 pins [form="♀ (female)"]
  D1 = Diode [package=diode-hv]
  J12 = female pin header, 2 pins [form="♀ (female)"]
  J13 = female pin header, 2 pins [form="♀ (female)"]
  J14 = female pin header, 4 pins [form="♀ (female)"]
  J15 = female pin header, 4 pins [form="♀ (female)"]

nets:
  N1: U1.RESET, R8.Pin_0, J7.pin1
  N2: U1.D1_(TX), J3.pin4
  N3: U1.D2, J2.pin1
  N4: U1.D3_(PWM), J3.pin5
  N5: U1.D4, R12.Pin_0
  N6: U1.VCC, U1.AVCC, C2.1, J3.pin2, J6.pin3
  N7: U1.GND, C2.2, TL431.B, J2.pin3, J3.pin1, R13.Pin_1, J6.pin1, J10.pin1, J11.pin3
  N8: U1.D5_(PWM), J2.pin2
  N9: U1.D7, J3.pin3
  N10: U1.D8, R1.Pin_1
  N11: U1.D9_(PWM), R4.Pin_1
  N12: U1.D10_(PWM), R2.Pin_1
  N13: U1.D11_(PWM), R5.Pin_1, J6.pin2
  N14: U1.D12, R3.Pin_1
  N15: U1.D13, R6.Pin_1
  N16: U1.AREF, C1.+
  N17: U1.A0, R1.Pin_0, R4.Pin_0, J10.pin4
  N18: U1.A1, R2.Pin_0, R5.Pin_0, J10.pin3
  N19: U1.A2, R3.Pin_0, R6.Pin_0, J10.pin2
  N20: U1.A3, J11.pin4
  N21: U1.A4, TL431.E, TL431.C
  N22: R12.Pin_1, R7.Pin_0, J2.pin4, C4.+, HT7350.C
  N23: C3.1, R14.Pin_1
  N24: R14.Pin_0, J11.pin1
  N25: HT7350.B, C5.+, D1.C
  N26: C5.-, J8.pin1
  N27: CD4048B2.J, CD4048B2.F, CD4048B2.C, CD4048B2.VDD, J14.pin4
  N28: CD4048B2.Kd, CD4048B2.G, CD4048B2.VSS, CD4048B2.Kc, CD4048B2.B, CD4048B2.EXPAND
  N29: CD4048B2.H, CD4048B2.Kb, CD4048B2.Ka, CD4048B2.A, J14.pin2
  N30: CD4048B2.E, CD4048B2.D, J14.pin3
  N31: J9.pin1, D1.A
  N32: J12.pin1, J13.pin2, J15.pin2, J15.pin3
  N33: J12.pin2, J15.pin4
  N34: J13.pin1, J15.pin1
